# Fritzing sketch main (saved by Fritzing 1.0.3b)

parts:
  Part1 = Arduino Uno (Rev3)
  A1 = RGB LED Strip Driver Module
  A2 = RGB Strip LED
  JACK1 = 2.1mm Barrel Jack with Terminal Block

nets:
  N1: Part1.D13/SCK, A1.Pin_4
  N2: Part1.GND, A1.Pin_1, A1.Pin_6, A1.Pin_10, JACK1.NEG
  N3: Part1.D3_PWM, A1.Pin_3
  N4: Part1.5V, A1.Pin_2
  N5: A1.Pin_5, A1.Pin_14, A2.Common_Connect, JACK1.POS
  N6: A1.Pin_11, A2.Blue_Connect
  N7: A1.Pin_12, A2.Red_Connect
  N8: A1.Pin_13, A2.Green_Connect

custom parts:
  RGB LED Strip Driver Module: RGB LED Strip Driver Module.
  RGB Strip LED: A tri-color Strip LED with red, green and blue. Pin order: red - common cathode - blue - green
